// Logisim project MIPSNew.circ as structural Verilog: 5 circuits, main circuit Reg32bits
module Reg32bits (
  input  [31:0] WriteData,
  input  CLK,
  input  RegWrite,
  input  [4:0] rSelect1,
  input  [4:0] wSelect,
  input  [4:0] rSelect2,
  output [31:0] ReadDataB,
  output [31:0] ReadData2
);

  wire and_1_out, and_2_out, and_3_out, and_4_out, and_5_out, and_6_out, and_7_out, and_8_out, and_9_out,
       and_10_out, and_11_out, and_12_out, and_13_out, and_14_out, and_15_out, and_16_out, and_17_out,
       and_18_out, and_19_out, and_20_out, and_21_out, and_22_out, and_23_out, and_24_out, and_25_out,
       and_26_out, and_27_out, and_28_out, and_29_out, and_30_out, and_31_out, decoder_1_out1,
       decoder_1_out2, decoder_1_out3, decoder_1_out4, decoder_1_out5, decoder_1_out6, decoder_1_out7,
       decoder_1_out8, decoder_1_out9, decoder_1_out10, decoder_1_out11, decoder_1_out12, decoder_1_out13,
       decoder_1_out14, decoder_1_out15, decoder_1_out16, decoder_1_out17, decoder_1_out18, decoder_1_out19,
       decoder_1_out20, decoder_1_out21, decoder_1_out22, decoder_1_out23, decoder_1_out24, decoder_1_out25,
       decoder_1_out26, decoder_1_out27, decoder_1_out28, decoder_1_out29, decoder_1_out30, decoder_1_out31;
  wire [31:0] register_1_q, register_2_q, register_3_q, register_4_q, register_5_q, register_6_q,
       register_7_q, register_8_q, register_9_q, register_10_q, register_11_q, register_12_q, register_13_q,
       register_14_q, register_15_q, register_16_q, register_17_q, register_18_q, register_19_q,
       register_20_q, register_21_q, register_22_q, register_23_q, register_24_q, register_25_q,
       register_26_q, register_27_q, register_28_q, register_29_q, register_30_q, register_31_q;

  Decoder #(.select(5), .enable("false")) decoder_1 (
    .out1(decoder_1_out1), .out2(decoder_1_out2), .out3(decoder_1_out3), .out4(decoder_1_out4),
    .out5(decoder_1_out5), .out6(decoder_1_out6), .out7(decoder_1_out7), .out8(decoder_1_out8),
    .out9(decoder_1_out9), .out10(decoder_1_out10), .out11(decoder_1_out11), .out12(decoder_1_out12),
    .out13(decoder_1_out13), .out14(decoder_1_out14), .out15(decoder_1_out15), .out16(decoder_1_out16),
    .out17(decoder_1_out17), .out18(decoder_1_out18), .out19(decoder_1_out19), .out20(decoder_1_out20),
    .out21(decoder_1_out21), .out22(decoder_1_out22), .out23(decoder_1_out23), .out24(decoder_1_out24),
    .out25(decoder_1_out25), .out26(decoder_1_out26), .out27(decoder_1_out27), .out28(decoder_1_out28),
    .out29(decoder_1_out29), .out30(decoder_1_out30), .out31(decoder_1_out31), .sel(wSelect));  // open: out0
  and and_1 (and_1_out, RegWrite, decoder_1_out1);
  and and_2 (and_2_out, RegWrite, decoder_1_out2);
  and and_3 (and_3_out, RegWrite, decoder_1_out3);
  and and_4 (and_4_out, RegWrite, decoder_1_out4);
  and and_5 (and_5_out, RegWrite, decoder_1_out5);
  and and_6 (and_6_out, RegWrite, decoder_1_out6);
  and and_7 (and_7_out, RegWrite, decoder_1_out7);
  and and_8 (and_8_out, RegWrite, decoder_1_out8);
  and and_9 (and_9_out, RegWrite, decoder_1_out9);
  and and_10 (and_10_out, RegWrite, decoder_1_out10);
  and and_11 (and_11_out, RegWrite, decoder_1_out11);
  and and_12 (and_12_out, RegWrite, decoder_1_out12);
  and and_13 (and_13_out, RegWrite, decoder_1_out13);
  and and_14 (and_14_out, RegWrite, decoder_1_out14);
  and and_15 (and_15_out, RegWrite, decoder_1_out15);
  and and_16 (and_16_out, RegWrite, decoder_1_out16);
  and and_17 (and_17_out, RegWrite, decoder_1_out17);
  and and_18 (and_18_out, RegWrite, decoder_1_out18);
  and and_19 (and_19_out, RegWrite, decoder_1_out19);
  and and_20 (and_20_out, RegWrite, decoder_1_out20);
  and and_21 (and_21_out, RegWrite, decoder_1_out21);
  and and_22 (and_22_out, RegWrite, decoder_1_out22);
  and and_23 (and_23_out, RegWrite, decoder_1_out23);
  and and_24 (and_24_out, RegWrite, decoder_1_out24);
  and and_25 (and_25_out, RegWrite, decoder_1_out25);
  and and_26 (and_26_out, RegWrite, decoder_1_out26);
  and and_27 (and_27_out, RegWrite, decoder_1_out27);
  and and_28 (and_28_out, RegWrite, decoder_1_out28);
  and and_29 (and_29_out, RegWrite, decoder_1_out29);
  and and_30 (and_30_out, RegWrite, decoder_1_out30);
  and and_31 (and_31_out, RegWrite, decoder_1_out31);
  Register #(.width(32)) register_1 (.D(WriteData), .en(and_4_out), .clk(CLK), .Q(register_1_q));  // open: clr
  Register #(.width(32)) register_2 (.D(WriteData), .en(and_8_out), .clk(CLK), .Q(register_2_q));  // open: clr
  Register #(.width(32)) register_3 (.D(WriteData), .en(and_12_out), .clk(CLK), .Q(register_3_q));  // open: clr
  Register #(.width(32)) register_4 (.D(WriteData), .en(and_16_out), .clk(CLK), .Q(register_4_q));  // open: clr
  Register #(.width(32)) register_5 (.D(WriteData), .en(and_20_out), .clk(CLK), .Q(register_5_q));  // open: clr
  Register #(.width(32)) register_6 (.D(WriteData), .en(and_24_out), .clk(CLK), .Q(register_6_q));  // open: clr
  Register #(.width(32)) register_7 (.D(WriteData), .en(and_28_out), .clk(CLK), .Q(register_7_q));  // open: clr
  Register #(.width(32)) register_8 (.D(WriteData), .en(and_1_out), .clk(CLK), .Q(register_8_q));  // open: clr
  Register #(.width(32)) register_9 (.D(WriteData), .en(and_5_out), .clk(CLK), .Q(register_9_q));  // open: clr
  Register #(.width(32)) register_10 (.D(WriteData), .en(and_9_out), .clk(CLK), .Q(register_10_q));  // open: clr
  Register #(.width(32)) register_11 (.D(WriteData), .en(and_13_out), .clk(CLK), .Q(register_11_q));  // open: clr
  Register #(.width(32)) register_12 (.D(WriteData), .en(and_17_out), .clk(CLK), .Q(register_12_q));  // open: clr
  Register #(.width(32)) register_13 (.D(WriteData), .en(and_21_out), .clk(CLK), .Q(register_13_q));  // open: clr
  Register #(.width(32)) register_14 (.D(WriteData), .en(and_25_out), .clk(CLK), .Q(register_14_q));  // open: clr
  Register #(.width(32)) register_15 (.D(WriteData), .en(and_29_out), .clk(CLK), .Q(register_15_q));  // open: clr
  Register #(.width(32)) register_16 (.D(WriteData), .en(and_2_out), .clk(CLK), .Q(register_16_q));  // open: clr
  Register #(.width(32)) register_17 (.D(WriteData), .en(and_6_out), .clk(CLK), .Q(register_17_q));  // open: clr
  Register #(.width(32)) register_18 (.D(WriteData), .en(and_10_out), .clk(CLK), .Q(register_18_q));  // open: clr
  Register #(.width(32)) register_19 (.D(WriteData), .en(and_14_out), .clk(CLK), .Q(register_19_q));  // open: clr
  Register #(.width(32)) register_20 (.D(WriteData), .en(and_18_out), .clk(CLK), .Q(register_20_q));  // open: clr
  Register #(.width(32)) register_21 (.D(WriteData), .en(and_22_out), .clk(CLK), .Q(register_21_q));  // open: clr
  Register #(.width(32)) register_22 (.D(WriteData), .en(and_26_out), .clk(CLK), .Q(register_22_q));  // open: clr
  Register #(.width(32)) register_23 (.D(WriteData), .en(and_30_out), .clk(CLK), .Q(register_23_q));  // open: clr
  Register #(.width(32)) register_24 (.D(WriteData), .en(and_3_out), .clk(CLK), .Q(register_24_q));  // open: clr
  Register #(.width(32)) register_25 (.D(WriteData), .en(and_7_out), .clk(CLK), .Q(register_25_q));  // open: clr
  Register #(.width(32)) register_26 (.D(WriteData), .en(and_11_out), .clk(CLK), .Q(register_26_q));  // open: clr
  Register #(.width(32)) register_27 (.D(WriteData), .en(and_15_out), .clk(CLK), .Q(register_27_q));  // open: clr
  Register #(.width(32)) register_28 (.D(WriteData), .en(and_19_out), .clk(CLK), .Q(register_28_q));  // open: clr
  Register #(.width(32)) register_29 (.D(WriteData), .en(and_23_out), .clk(CLK), .Q(register_29_q));  // open: clr
  Register #(.width(32)) register_30 (.D(WriteData), .en(and_27_out), .clk(CLK), .Q(register_30_q));  // open: clr
  Register #(.width(32)) register_31 (.D(WriteData), .en(and_31_out), .clk(CLK), .Q(register_31_q));  // open: clr
  Multiplexer #(.select(5), .width(32), .enable("false")) multiplexer_1 (
    .in0({32{1'b0}}), .in1(register_8_q), .in2(register_16_q), .in3(register_24_q), .in4(register_1_q),
    .in5(register_9_q), .in6(register_17_q), .in7(register_25_q), .in8(register_2_q), .in9(register_10_q),
    .in10(register_18_q), .in11(register_26_q), .in12(register_3_q), .in13(register_11_q),
    .in14(register_19_q), .in15(register_27_q), .in16(register_4_q), .in17(register_12_q),
    .in18(register_20_q), .in19(register_28_q), .in20(register_5_q), .in21(register_13_q),
    .in22(register_21_q), .in23(register_29_q), .in24(register_6_q), .in25(register_14_q),
    .in26(register_22_q), .in27(register_30_q), .in28(register_7_q), .in29(register_15_q),
    .in30(register_23_q), .in31(register_31_q), .out(ReadDataB), .sel(rSelect1));
  Multiplexer #(.select(5), .width(32), .enable("false")) multiplexer_2 (
    .in0({32{1'b0}}), .in1(register_8_q), .in2(register_16_q), .in3(register_24_q), .in4(register_1_q),
    .in5(register_9_q), .in6(register_17_q), .in7(register_25_q), .in8(register_2_q), .in9(register_10_q),
    .in10(register_18_q), .in11(register_26_q), .in12(register_3_q), .in13(register_11_q),
    .in14(register_19_q), .in15(register_27_q), .in16(register_4_q), .in17(register_12_q),
    .in18(register_20_q), .in19(register_28_q), .in20(register_5_q), .in21(register_13_q),
    .in22(register_21_q), .in23(register_29_q), .in24(register_6_q), .in25(register_14_q),
    .in26(register_22_q), .in27(register_30_q), .in28(register_7_q), .in29(register_15_q),
    .in30(register_23_q), .in31(register_31_q), .out(ReadData2), .sel(rSelect2));
endmodule

module Mips (
  input  [31:0] PCADD,
  input  [4:0] shift,
  input  [4:0] shift_2,
  input  in_4,
  input  EnablePC,
  output error,
  output [31:0] WriteData,
  output [31:0] out_8,
  output regWrite,
  output [31:0] WriteData_2,
  output [4:0] wSelect,
  output [31:0] out_12,
  output [23:0] out_13
);

  wire alu_1_p1, and_1_out, clock_1_out, clock_2_out, clock_3_out, controlunit_1_alusrc,
       controlunit_1_branch, controlunit_1_jump, controlunit_1_memread, controlunit_1_memtoreg,
       controlunit_1_memwrite, controlunit_1_op0, controlunit_1_op1, controlunit_1_regdst;
  wire [3:0] alucontrol_1_aluinput;
  wire [7:0] alu_1_p2;
  wire [27:0] bit_extender_1_out, shifter_1_out;
  wire [31:0] adder_1_out, bit_extender_2_out, counter_1_q, multiplexer_2_out, multiplexer_3_out,
       multiplexer_4_out, ram_1_dout, reg32bits_1_readdatab, shifter_2_out;

  Clock clock_1 (.out(clock_1_out));
  Counter #(.width(32), .max('hffffffff)) counter_1 (
    .clr(in_4), .load(EnablePC), .up(EnablePC), .count(in_4), .clk(clock_1_out), .D(multiplexer_4_out),
    .Q(counter_1_q));  // open: carry
  Adder #(.width(32)) adder_1 (.a(PCADD), .b(counter_1_q), .out(adder_1_out));  // open: cin, cout
  ROM #(.addrWidth(24), .dataWidth(32)) rom_1 (.addr(counter_1_q[23:0]), .data(out_12));
  assign bit_extender_1_out = {{2{out_12[25]}}, out_12[25:0]};  // Bit_Extender bit_extender_1
  Shifter #(.width(28)) shifter_1 (.in(bit_extender_1_out), .\dist (shift), .out(shifter_1_out));
  controlUnit controlunit_1 (
    .ERROR_O(error), .OP1(controlunit_1_op1), .OP0(controlunit_1_op0), .RegDst(controlunit_1_regdst),
    .Jump(controlunit_1_jump), .Branch(controlunit_1_branch), .MemRead(controlunit_1_memread),
    .MemtoReg(controlunit_1_memtoreg), .MemWrite(controlunit_1_memwrite), .ALUSrc(controlunit_1_alusrc),
    .RegWrite(regWrite));  // open: ins3126
  assign bit_extender_2_out = {{16{out_12[15]}}, out_12[15:0]};  // Bit_Extender bit_extender_2
  Multiplexer #(.width(5), .enable("false")) multiplexer_1 (
    .in0(out_12[20:16]), .in1(out_12[15:11]), .out(wSelect), .sel(controlunit_1_regdst));
  Clock clock_2 (.out(clock_2_out));
  Reg32bits reg32bits_1 (
    .WriteData(WriteData_2), .RegWrite(regWrite), .wSelect(wSelect), .ReadDataB(reg32bits_1_readdatab),
    .ReadData2(out_8), .rSelect1(out_12[25:21]), .rSelect2(out_12[20:16]), .CLK(clock_2_out));
  Multiplexer #(.width(32), .enable("false")) multiplexer_2 (
    .in0(out_8), .in1(bit_extender_2_out), .out(multiplexer_2_out), .sel(controlunit_1_alusrc));
  Shifter #(.width(32)) shifter_2 (.in(bit_extender_2_out), .\dist (shift_2), .out(shifter_2_out));
  ALUControl alucontrol_1 (.ALUInput(alucontrol_1_aluinput));  // open: ALUOP0, ALUOP1, funct
  Adder #(.width(32)) adder_2 (.a(adder_1_out), .b(shifter_2_out), .out(WriteData));  // open: cin, cout
  // ALU alu_1: pin names not known; wires that end beside it: alu_1_p1, {alu_1_p2, out_13}
  Clock clock_3 (.out(clock_3_out));
  and and_1 (and_1_out, controlunit_1_branch, alu_1_p1);
  RAM #(.addrWidth(24), .dataWidth(32), .databus("bibus")) ram_1 (
    .addr(out_13), .we(controlunit_1_memwrite), .oe(controlunit_1_memread), .clk(clock_3_out), .din(out_8),
    .dout(ram_1_dout));
  Multiplexer #(.width(32), .enable("false")) multiplexer_3 (
    .in0(adder_1_out), .in1(WriteData), .out(multiplexer_3_out), .sel(and_1_out));
  Multiplexer #(.width(32), .enable("false")) multiplexer_4 (
    .in0(multiplexer_3_out), .in1({adder_1_out[31:28], shifter_1_out}), .out(multiplexer_4_out),
    .sel(controlunit_1_jump));
  Multiplexer #(.width(32), .enable("false")) multiplexer_5 (
    .in0({alu_1_p2, out_13}), .in1(ram_1_dout), .out(WriteData_2), .sel(controlunit_1_memtoreg));

  // Notes on the sheet:
  //   contents of rom_1 (hex, n*v repeats v):
  //   4*0 8c020000 0 0 0 21b20 0 0 0 10430001 6*0 8000001 8000001
  //   25-0
  //   16-0
  //   31-26
  //   15-11
  //   10-6
  //   5-0
  //   20-16
  //   25-21
  //   Alusrc
  //   MemWrite
  //   MemRead
  //   Jump
  //   MemtoReg
  //   op0
  //   op1
  //   branch
  //   readdata1
  //   readdata2
  //   zero
  //   ALUOP
endmodule

module ALU (
  input  [31:0] A,
  input  [31:0] B,
  input  [3:0] Operation,
  output Zero,
  output [31:0] Result
);

  wire or_2_out, or_3_out, or_4_out, or_5_out;
  wire [31:0] adder_1_out, and_1_out, multiplexer_1_out, not_1_out, or_1_out;

  assign not_1_out = ~B;  // NOT_Gate not_1, 32 bits wide
  Multiplexer #(.width(32), .enable("false")) multiplexer_1 (
    .in0(B), .in1(not_1_out), .out(multiplexer_1_out), .sel(Operation[2]));
  assign and_1_out = A & multiplexer_1_out;  // AND_Gate and_1, 32 bits wide
  assign or_1_out = A | multiplexer_1_out;  // OR_Gate or_1, 32 bits wide
  Adder #(.width(32)) adder_1 (.a(A), .b(multiplexer_1_out), .out(adder_1_out), .cin(Operation[2]));  // open: cout
  Multiplexer #(.select(2), .width(32), .enable("false")) multiplexer_2 (
    .in0(and_1_out), .in1(or_1_out), .in2(adder_1_out), .out(Result), .sel(Operation[1:0]));  // open: in3
  or or_2 (or_2_out, Result[0], Result[1], Result[2], Result[3], Result[4], Result[5], Result[6]);
  or or_3 (or_3_out, Result[7], Result[8], Result[9], Result[10], Result[11], Result[12], Result[13], Result[14], Result[15]);
  or or_4 (or_4_out, Result[16], Result[17], Result[18], Result[19], Result[20], Result[21], Result[22], Result[23], Result[24]);
  or or_5 (or_5_out, Result[25], Result[26], Result[27], Result[28], Result[29], Result[30], Result[31]);
  nor nor_1 (Zero, or_2_out, or_3_out, or_4_out, or_5_out);
endmodule

module controlUnit (
  input  [5:0] ins3126,
  output ERROR_O,
  output OP1,
  output OP0,
  output RegDst,
  output Jump,
  output Branch,
  output MemRead,
  output MemtoReg,
  output MemWrite,
  output ALUSrc,
  output RegWrite
);

  wire Addi_out, BEQ_out, BNE_out;

  and R_type (OP1, ~ins3126[5], ~ins3126[4], ~ins3126[3], ~ins3126[2], ~ins3126[1], ~ins3126[0]);  // AND_Gate
  and LW (MemRead, ins3126[5], ~ins3126[4], ~ins3126[3], ~ins3126[2], ins3126[1], ins3126[0]);  // AND_Gate
  and SW (MemWrite, ins3126[5], ~ins3126[4], ins3126[3], ~ins3126[2], ins3126[1], ins3126[0]);  // AND_Gate
  or or_1 (Branch, BEQ_out, BNE_out);
  and BEQ (BEQ_out, ~ins3126[5], ~ins3126[4], ~ins3126[3], ins3126[2], ~ins3126[1], ~ins3126[0]);  // AND_Gate
  and BNE (BNE_out, ins3126[5], ins3126[4], ins3126[3], ~ins3126[2], ins3126[1], ins3126[0]);  // AND_Gate
  and Addi (Addi_out, ~ins3126[5], ~ins3126[4], ins3126[3], ~ins3126[2], ~ins3126[1], ~ins3126[0]);  // AND_Gate
  and J (Jump, ~ins3126[5], ~ins3126[4], ~ins3126[3], ~ins3126[2], ins3126[1], ~ins3126[0]);  // AND_Gate
  or or_2 (ALUSrc, Addi_out, MemRead, MemWrite);
  and and_1 (ERROR_O, ~OP1, ~MemRead, ~MemWrite, ~BEQ_out, ~BNE_out, ~Addi_out, ~Jump);  // AND_Gate
  or or_3 (RegWrite, OP1, Addi_out, MemRead);

  assign MemtoReg = MemRead;
  assign OP0 = Branch;
  assign RegDst = OP1;
endmodule

module ALUControl (
  input  ALUOP0,
  input  ALUOP1,
  input  [5:0] funct,
  output [3:0] ALUInput
);

  wire and_1_out, or_1_out;
  wire [2:0] and_2_out;

  or or_1 (or_1_out, funct[3], funct[0]);
  and and_1 (and_1_out, ALUOP1, funct[1]);
  and and_2 (and_2_out[0], ALUOP1, or_1_out);
  or or_2 (and_2_out[2], ALUOP0, and_1_out);
  or or_3 (and_2_out[1], ~ALUOP1, ~funct[2]);  // OR_Gate
  assign ALUInput = {{1{1'b0}}, and_2_out};  // Bit_Extender bit_extender_1

  // Notes on the sheet:
  //   5-0
endmodule
